// Logisim project homework3_beadenkopf.circ as structural Verilog: 1 circuit, main circuit main
module main (
  input  Gate_A,
  input  Gate_B,
  output out_3
);

  or or_1 (out_3, Gate_A, Gate_A, Gate_B, Gate_B);

  // Notes on the sheet:
  //   Homework 3
endmodule
